# Fritzing sketch wisetag (saved by Fritzing 0.9.2b)

parts:
  D1 = LTE-302 [part_number=TSAL6100 package=lte-302]
  Part1 = Arduino Uno (Rev3)
  R2 = Resistor [tolerance=±5% resistance=100 package=THT]
  S1 = Pushbutton [package="[THT]"]
  IR1 = TSOP312.., 314.. [package=THT]
  R1 = Resistor [tolerance=±5% resistance=100 package=THT]
  J1 = Piezo Speaker

nets:
  N1: D1.C, Part1.D2
  N2: Part1.D12/MISO, IR1.Data
  N3: Part1.D3_PWM, R2.Pin_1
  N4: Part1.D4, J1.pin2
  N5: Part1.5V, S1.Pin_3, S1.Pin_4, IR1.Vs
  GND: Part1.GND, IR1.GND, R1.Pin_0, J1.pin1
